// Logisim project LAB-C6-correct.circ as structural Verilog: 1 circuit, main circuit main
module main (
  input  CLK,
  input  CLR_N,
  input  EN,
  output [3:0] Q
);

  wire n1;

  not not_1 (n1, CLR_N);
  Counter #(.width(4), .max('h5), .ongoal("wrap")) counter_1 (
    .load(1'b0), .D(4'b0000), .count(EN), .Q(Q), .up(1'b1), .clk(CLK), .clr(n1));  // open: carry
endmodule
