// Logisim project LAB-D-correct.circ as structural Verilog: 1 circuit, main circuit main
module main (
  input  CLK,
  input  CLR_N,
  input  PRE_N,
  input  D,
  output Q
);

  wire n1, n2;

  not not_1 (n1, CLR_N);
  not not_2 (n2, PRE_N);
  D_Flip_Flop #(.trigger("rising")) d_ff_1 (.clk(CLK), .D(D), .Q(Q), .preset(n2), .reset(n1));  // open: Qn
endmodule
