// Logisim project LAB-FSM-wrong.circ as structural Verilog: 1 circuit, main circuit main
module main (
  input  CLK,
  input  CLR_N,
  output [1:0] Q
);

  wire n1, n2;

  not not_1 (n1, CLR_N);
  not not_2 (n2, Q[1]);
  D_Flip_Flop #(.trigger("rising")) d_ff_1 (.clk(CLK), .D(n2), .Qn(Q[0]), .preset(1'b0), .reset(n1));  // open: Q
  D_Flip_Flop #(.trigger("rising")) d_ff_2 (.clk(CLK), .D(Q[0]), .Qn(Q[1]), .preset(1'b0), .reset(n1));  // open: Q
endmodule
