// Logisim project LAB-S4-correct.circ as structural Verilog: 1 circuit, main circuit main
module main (
  input  CLK,
  input  CLR_N,
  input  S1,
  input  S0,
  input  SR,
  input  SL,
  input  [3:0] P,
  output [3:0] Q
);

  wire n1, n2, n3, n4, n5, n6, n7, n8, n9, n10, n11, n12, n13, n14, n15, n16, n17, n18, n19, n20, n21, n22,
       n23, n24, n25, n26, n27, n28, n29, n30, n31, n32, n33, n34, n35;

  not not_1 (n1, CLR_N);
  not not_2 (n2, S1);
  not not_3 (n3, S0);
  and and_1 (n4, n2, n3);
  and and_2 (n5, n2, S0);
  and and_3 (n6, S1, n3);
  and and_4 (n7, S1, S0);
  and and_5 (n8, n4, Q[0]);
  and and_6 (n9, n5, Q[1]);
  and and_7 (n10, n6, SL);
  and and_8 (n11, n7, P[0]);
  or or_1 (n12, n8, n9);
  or or_2 (n13, n10, n11);
  or or_3 (n14, n12, n13);
  D_Flip_Flop #(.trigger("rising")) d_ff_1 (.clk(CLK), .D(n14), .Q(Q[0]), .preset(1'b0), .reset(n1));  // open: Qn
  and and_9 (n15, n4, Q[1]);
  and and_10 (n16, n5, Q[2]);
  and and_11 (n17, n6, Q[0]);
  and and_12 (n18, n7, P[1]);
  or or_4 (n19, n15, n16);
  or or_5 (n20, n17, n18);
  or or_6 (n21, n19, n20);
  D_Flip_Flop #(.trigger("rising")) d_ff_2 (.clk(CLK), .D(n21), .Q(Q[1]), .preset(1'b0), .reset(n1));  // open: Qn
  and and_13 (n22, n4, Q[2]);
  and and_14 (n23, n5, Q[3]);
  and and_15 (n24, n6, Q[1]);
  and and_16 (n25, n7, P[2]);
  or or_7 (n26, n22, n23);
  or or_8 (n27, n24, n25);
  or or_9 (n28, n26, n27);
  D_Flip_Flop #(.trigger("rising")) d_ff_3 (.clk(CLK), .D(n28), .Q(Q[2]), .preset(1'b0), .reset(n1));  // open: Qn
  and and_17 (n29, n4, Q[3]);
  and and_18 (n30, n5, SR);
  and and_19 (n31, n6, Q[2]);
  and and_20 (n32, n7, P[3]);
  or or_10 (n33, n29, n30);
  or or_11 (n34, n31, n32);
  or or_12 (n35, n33, n34);
  D_Flip_Flop #(.trigger("rising")) d_ff_4 (.clk(CLK), .D(n35), .Q(Q[3]), .preset(1'b0), .reset(n1));  // open: Qn
endmodule
